# Fritzing sketch switch (saved by Fritzing 0.9.2b)
breadboards: 1

parts:
  Raspberry_Pi1 = Raspberry Pi 2
  LED1 = smd LED [color="Red (633nm)" package="0805 [SMD]"]
  R1 = Resistor [tolerance=±5% resistance=220 package=THT]
  S1 = Momentary Switch [package=ksa_sealed_tac_switch]
  R2 = Resistor [tolerance=±5% resistance=220 package=THT]

nets:
  N1: Raspberry_Pi1.3v3, R2.Pin_0
  N2: Raspberry_Pi1.GPIO24, S1.2
  N3: Raspberry_Pi1.GPIO18, R1.Pin_1
  N4: Raspberry_Pi1.GND, LED1.cathode
  N5: LED1.anode, R1.Pin_0
  N6: S1.4, R2.Pin_1
