# Fritzing sketch sound (saved by Fritzing 0.9.2b)
breadboards: 1

parts:
  Raspberry_Pi1 = Raspberry Pi 2
  J1 = Piezo Speaker

nets:
  N1: Raspberry_Pi1.GPIO23, J1.pin2
  N2: Raspberry_Pi1.GND, J1.pin1
