# Fritzing sketch TemperatureHumidity (saved by Fritzing 0.9.2b)
breadboards: 1

parts:
  DHT1 = DHT11 Humitidy and Temperature Sensor
  R1 = Resistor [tolerance=±5% resistance=220 package=THT]
  Raspberry_Pi1 = Raspberry Pi 2

nets:
  VDD: DHT1.VDD, R1.Pin_0, Raspberry_Pi1.5V
  N1: DHT1.DATA, R1.Pin_1, Raspberry_Pi1.GPIO23
  GND: DHT1.GND, Raspberry_Pi1.GND

custom parts:
  DHT11 Humitidy and Temperature Sensor: DHT11 Humidity and Temperature Sensor
