# Fritzing sketch isr (saved by Fritzing 0.9.2b)
breadboards: 1

parts:
  Raspberry_Pi1 = Raspberry Pi 2
  S1 = Momentary Switch [package=ksa_sealed_tac_switch]
  R2 = Resistor [tolerance=±5% resistance=220 package=THT]

nets:
  N1: Raspberry_Pi1.3v3, S1.4
  N2: Raspberry_Pi1.GPIO23, S1.1
  N3: Raspberry_Pi1.GND, R2.Pin_1
  N4: S1.2, R2.Pin_0
