# Fritzing sketch RTC (saved by Fritzing 0.9.2b)
breadboards: 1

parts:
  Raspberry_Pi1 = Raspberry Pi 2
  RTC1 = DS1307 RTC Breakout

nets:
  3V3: Raspberry_Pi1.3v3, RTC1.5V
  N1: Raspberry_Pi1.GPIO2, RTC1.SDA
  N2: Raspberry_Pi1.GPIO3, RTC1.SCL
  GND: Raspberry_Pi1.GND, RTC1.GND

custom parts:
  DS1307 RTC Breakout: DS1307 Real-time Clock Breakout Board with Battery
