# Fritzing sketch servo (saved by Fritzing 0.9.2b)

parts:
  Raspberry_Pi1 = Raspberry Pi 2
  J1 = Basic Servo
  VCC1 = Battery

nets:
  GND: Raspberry_Pi1.GND, J1.gnd, VCC1.-
  N1: Raspberry_Pi1.GPIO24, J1.pulse
