# Fritzing sketch oled (saved by Fritzing 0.9.2b)

parts:
  Raspberry_Pi1 = Raspberry Pi 2
  OLED1 = 128x64 Monochrom OLED Display with SPI Control

nets:
  N1: Raspberry_Pi1.GPIO2, OLED1.Data
  N2: Raspberry_Pi1.GPIO3, OLED1.Clock
  N3: Raspberry_Pi1.GPIO25, OLED1.Reset
  GND: Raspberry_Pi1.GND, OLED1.GND
  5V: Raspberry_Pi1.5V, OLED1.Vin
